# Fritzing sketch circuit (saved by Fritzing 0.9.3b)

parts:
  Part1 = Arduino Uno (Rev3)
  PIR1 = PIR sensor
  Part2 = KY-012 Active Buzzer Module [package="Breakout board"]

nets:
  N1: Part1.D5_PWM, PIR1.SIG
  N2: Part1.3V3, Part2.S
  5V: Part1.5V, PIR1.VDD
  GND: Part1.GND, PIR1.GND
  N3: Part1.VIN, Part2.-

custom parts:
  KY-012 Active Buzzer Module: Active Piezoelectric Buzzer Module Keyes KY-012, it produces single-tone sound when signal is high.
